// Digital circuit computer.dig as structural Verilog
module computer (
  input  Speed,
  input  Clock_On,
  input  [31:0] p_0,
  input  [31:0] p_1,
  input  [31:0] p_2,
  input  [31:0] p_3,
  input  [63:0] Instruction,
  output [31:0] r_5,
  output [23:0] A_r
);

  wire _32_bit_adder_1_c_out, _32_bit_right_1_p2, and_1_out, and_2_out, generic_switch_1_out,
       generic_switch_2_out, generic_switch_3_out, generic_switch_4_out, generic_switch_6_out, or_1_out,
       or_2_out, or_3_out, Step_out;
  wire [1:0] generic_down_conversion_1_p2;
  wire [4:0] generic_down_conversion_2_p2, register_1_q;
  wire [23:0] register_2_q;
  wire [31:0] _4x_32_bit_switch_1_p_out, _5_32_register_switch_1_out, _32_bit_adder_1_s_out,
       _32_bit_left_1_out, generic_switch_5_out, ramdualport_1_d, register_3_q, register_4_q, register_5_q;
  wire [31:24] register_2_q_2;

  ROM #(.AddrBits(24), .isProgramMemory("true"), .Bits(64)) rom_1 ();  // open: A, sel, D
  CounterPreset #(.Bits(24)) counterpreset_1 (
    .en(1'b1), .C(or_1_out), .dir(1'b0), .in(register_2_q), .ld(or_2_out), .clr(Instruction[38]), .out(A_r));  // open: ovf
  and and_1 (and_1_out, Speed, Clock_On);
  Button Step (.out(Step_out));
  or or_1 (or_1_out, and_1_out, Step_out);
  or or_2 (or_2_out, and_2_out, Instruction[39]);
  Break break_1 (.brk(or_1_out));
  and and_2 (and_2_out, register_3_q[0], Instruction[47]);
  or or_3 (or_3_out, Instruction[44], Instruction[45]);
  generic_switch #(.generic("bitWidth := 32;")) generic_switch_1 (
    .A(Instruction[31:0]), .B(ramdualport_1_d), .C(Instruction[42]), .Out(generic_switch_1_out));
  generic_switch #(.generic("bitWidth := 32;")) generic_switch_2 (
    .A(generic_switch_1_out), .B(_5_32_register_switch_1_out), .C(Instruction[43]), .Out(generic_switch_2_out));
  generic_switch #(.generic("bitWidth := 32;")) generic_switch_3 (
    .A(generic_switch_2_out), .B(generic_switch_6_out), .C(or_3_out), .Out(generic_switch_3_out));
  generic_switch #(.generic("bitWidth := 32;")) generic_switch_4 (
    .A(generic_switch_3_out), .B(_32_bit_adder_1_s_out), .C(Instruction[46]), .Out(generic_switch_4_out));
  Register #(.Bits(5)) register_1 (
    .D(generic_down_conversion_2_p2), .C(or_1_out), .en(Instruction[37]), .Q(register_1_q));
  generic_switch #(.generic("bitWidth := 32;")) generic_switch_5 (
    .A(generic_switch_4_out), .B(_4x_32_bit_switch_1_p_out), .C(Instruction[41]), .Out(generic_switch_5_out));
  // generic_down_conversion #(.generic("InBits := 5; OutBits := 2;")) generic_down_conversion_1: pin names not known; wires that end beside it: register_1_q, generic_down_conversion_1_p2
  _4x_32_bit_switch _4x_32_bit_switch_1 (
    .Address(generic_down_conversion_1_p2), .p_0(p_0), .p_1(p_1), .p_2(p_2), .p_3(p_3),
    .p_out(_4x_32_bit_switch_1_p_out));
  // generic_down_conversion #(.generic("InBits := 32; OutBits := 5;")) generic_down_conversion_2: pin names not known; wires that end beside it: generic_switch_5_out, generic_down_conversion_2_p2
  Register #(.Bits(32)) register_2 (
    .D(generic_switch_5_out), .C(or_1_out), .en(Instruction[32]), .Q({register_2_q_2, register_2_q}));
  Register #(.Bits(32)) register_3 (.D(generic_switch_5_out), .C(or_1_out), .en(Instruction[33]), .Q(register_3_q));
  Register #(.Bits(32)) register_4 (.D(generic_switch_5_out), .C(or_1_out), .en(Instruction[34]), .Q(register_4_q));
  Register #(.Bits(32)) register_5 (.D(generic_switch_5_out), .C(or_1_out), .en(Instruction[35]), .Q(register_5_q));
  Register #(.Bits(32)) register_6 (.D(generic_switch_5_out), .C(or_1_out), .en(Instruction[36]), .Q(r_5));
  _32_bit_left _32_bit_left_1 (.in({register_2_q_2, register_2_q}), .out(_32_bit_left_1_out));
  // _32_bit_right #(.generic("Bits := 32;")) _32_bit_right_1: pin names not known; wires that end beside it: {register_2_q_2, register_2_q}, _32_bit_right_1_p2
  _5_32_register_switch _5_32_register_switch_1 (
    .In_1({register_2_q_2, register_2_q}), .In_2(register_3_q), .In_3(register_4_q), .In_4(register_5_q),
    .In_5(r_5), .A(register_1_q), .Out(_5_32_register_switch_1_out));
  generic_switch #(.generic("bitWidth := 32;")) generic_switch_6 (
    .A(_32_bit_left_1_out), .B(_32_bit_right_1_p2), .C(Instruction[44]), .Out(generic_switch_6_out));
  // Probe on register_5_q
  // Probe Reg_1 on {register_2_q_2, register_2_q}
  // Probe Reg_2 on register_3_q
  _32_bit_adder _32_bit_adder_1 (
    .A({register_2_q_2, register_2_q}), .B(register_3_q), .C_in(1'b0), .Mode(register_4_q[0]),
    .C_out(_32_bit_adder_1_c_out), .S_out(_32_bit_adder_1_s_out));
  // Probe Reg_3 on register_4_q[0]
  // Probe on _32_bit_adder_1_c_out
  RAMDualPort #(.AddrBits(24), .Bits(32)) ramdualport_1 (
    .A(register_3_q[23:0]), .Din({register_2_q_2, register_2_q}), .str(Instruction[40]), .C(or_1_out),
    .ld(Instruction[42]), .D(ramdualport_1_d));
  // Probe Out on _32_bit_adder_1_s_out
  // Probe Out on ramdualport_1_d
  // Pins of 1 and 64 bits meet at Instruction

  // Notes on the sheet:
  //   Speed: Hz: 50
  //   A_r: ROM address
  //   contents of rom_1 (hex, n*v repeats v):
  //   800000000,200000001,2000000008,0,80100000000,400800000000,100000003
  //   ,8000000000,4000000000,4000000000
endmodule
