// Digital circuit system.dig as structural Verilog
module system (
  input  clk,
  input  [31:0] in_2
);

  wire computer_1_p8, dipswitch_1_out, dipswitch_2_out;
  wire [23:0] computer_1_p9;
  wire [63:0] rom_1_d;

  ROM #(.AddrBits(24), .Bits(64)) rom_1 (.A(computer_1_p9), .sel(dipswitch_1_out), .D(rom_1_d));
  DipSwitch #(.dipDefault("true")) dipswitch_1 (.out(dipswitch_1_out));
  DipSwitch dipswitch_2 (.out(dipswitch_2_out));
  // computer computer_1: pin names not known; wires that end beside it: clk, dipswitch_2_out, in_2, {32{1'b0}}, {32{1'b0}}, {32{1'b0}}, rom_1_d, computer_1_p8, computer_1_p9
  // Probe on computer_1_p8
endmodule
